# Fritzing sketch MODULO RELE 4 CANAIS COM BLUETOOTH-Ponte H-final (saved by Fritzing 0.9.3b)
circuit board: 13.5cm x 9cm
breadboards: 4

parts:
  BLUETOOTH = Bluetooth HC-06u [package=THT]
  SEG5 = Relay T73
  FRENTE = Relay T73
  D2 = Rectifier Diode [part_number=1N4007 package="300 mil [THT]"]
  Q1 = TRANSISTOR_NPN [part_number=BC548 package=to-92-ammo]
  R2 = Resistor [tolerance=±5% resistance=330 package=THT]
  R1 = Resistor [tolerance=±5% resistance=1k package=THT]
  J20 = Screw terminal - 2 pins [package=THT]
  ENTRADA_F/R = Relay T73
  D1 = Rectifier Diode [part_number=1N4007 package="300 mil [THT]"]
  J21 = Screw terminal - 2 pins [package=THT]
  RE = Relay T73
  FRENTE6 = Relay T73
  D3 = Rectifier Diode [part_number=1N4007 package="300 mil [THT]"]
  D4 = Rectifier Diode [part_number=1N4007 package="300 mil [THT]"]
  Q2 = TRANSISTOR_NPN [part_number=BC548 package=to-92-ammo]
  R4 = Resistor [tolerance=±5% resistance=330 package=THT]
  R3 = Resistor [tolerance=±5% resistance=1k package=THT]
  J22 = Screw terminal - 2 pins [package=THT]
  J23 = Screw terminal - 2 pins [package=THT]
  Arduino_Nano = Arduino Nano (Rev3.0)
  SEG6 = Relay T73
  FRENTE7 = Relay T73
  Entrada_D/E = Relay T73
  Esquerda = Relay T73
  Direita = Relay T73
  D6 = Rectifier Diode [part_number=1N4007 package="300 mil [THT]"]
  D7 = Rectifier Diode [part_number=1N4007 package="300 mil [THT]"]
  D5 = Rectifier Diode [part_number=1N4007 package="300 mil [THT]"]
  D8 = Rectifier Diode [part_number=1N4007 package="300 mil [THT]"]
  Q3 = TRANSISTOR_NPN [part_number=BC548 package=to-92-ammo]
  R5 = Resistor [tolerance=±5% resistance=330 package=THT]
  R7 = Resistor [tolerance=±5% resistance=330 package=THT]
  R8 = Resistor [tolerance=±5% resistance=1k package=THT]
  R6 = Resistor [tolerance=±5% resistance=1k package=THT]
  J24 = Screw terminal - 2 pins [package=THT]
  J25 = Screw terminal - 2 pins [package=THT]
  J26 = Screw terminal - 2 pins [package=THT]
  Q4 = TRANSISTOR_NPN [part_number=BC548 package=to-92-ammo]
  L18 = smd LED [color="Green (555nm)" package="0603 [SMD]"]
  L19 = smd LED [color="Green (555nm)" package="0603 [SMD]"]
  L17 = smd LED [color="Green (555nm)" package="0603 [SMD]"]
  L20 = smd LED [color="Green (555nm)" package="0603 [SMD]"]
  D9 = Rectifier Diode [part_number=1N4007 package="300 mil [THT]"]
  D10 = Rectifier Diode [part_number=1N4007 package="300 mil [THT]"]

nets:
  VCC: BLUETOOTH.VCC, FRENTE.C1, D2.cathode, ENTRADA_F/R.C2, D1.cathode, RE.C1, FRENTE6.C2, D3.cathode, D4.cathode, Arduino_Nano.5V, FRENTE7.C1, Entrada_D/E.C1, Esquerda.C2, Direita.C2, D6.cathode, D7.cathode, D5.cathode, D8.cathode
  GND: BLUETOOTH.GND, SEG5.C1, Q1.C, Q2.C, J23.pin2, Arduino_Nano.GND, SEG6.C1, Q3.C, Q4.C, L18.cathode, L19.cathode, L17.cathode, L20.cathode, D9.anode, D10.anode
  N1: BLUETOOTH.TXD, Arduino_Nano.D3
  N2: SEG5.C2, Q2.B, R4.Pin_1, R3.Pin_1, Arduino_Nano.D11/MOSI, D9.cathode
  N3: SEG5.COM, Arduino_Nano.D12/MISO
  N4: SEG5.NC, Q1.B, R2.Pin_1, R1.Pin_1
  N5: FRENTE.C2, D2.anode, Q1.E, R1.Pin_0, ENTRADA_F/R.C1, D1.anode
  N6: FRENTE.COM, J20.pin1, FRENTE6.COM
  N7: FRENTE.NO, J21.pin1
  N8: R2.Pin_0, L17.anode
  N9: J20.pin2, ENTRADA_F/R.COM, RE.COM
  N10: ENTRADA_F/R.NO, J21.pin2
  N11: RE.C2, FRENTE6.C1, D3.anode, D4.anode, Q2.E, R3.Pin_0
  N12: RE.NO, J22.pin1
  N13: FRENTE6.NO, J22.pin2
  N14: R4.Pin_0, L18.anode
  N15: J23.pin1, Arduino_Nano.VIN
  N16: Arduino_Nano.D9, SEG6.C2, Q3.B, R5.Pin_1, R6.Pin_1, D10.cathode
  N17: Arduino_Nano.D10, SEG6.COM
  N18: SEG6.NC, R7.Pin_1, R8.Pin_1, Q4.B
  N19: FRENTE7.C2, Direita.C1, D6.anode, D5.anode, Q3.E, R6.Pin_0
  N20: FRENTE7.COM, Esquerda.COM, J25.pin2
  N21: FRENTE7.NO, J24.pin1
  N22: Entrada_D/E.C2, Esquerda.C1, D7.anode, D8.anode, R8.Pin_0, Q4.E
  N23: Entrada_D/E.COM, Direita.COM, J25.pin1
  N24: Entrada_D/E.NO, J26.pin1
  N25: Esquerda.NO, J26.pin2
  N26: Direita.NO, J24.pin2
  N27: R5.Pin_0, L19.anode
  N28: R7.Pin_0, L20.anode

notes:
  Entrada Motor F/R
  Saída F
  Saída R
  Entrada Motor D/E
  Saída D
  -  + <-ALIMENTACAO(9~12V)

custom parts:
  Bluetooth HC-06u: Bluetooth HC-06 - face up, pins down 16.5mm x 37.5mm PCB
  Relay T73: An T73 Mini PCB Relay
